# Fritzing sketch Heart_Rate_Monitor_demo (saved by Fritzing 0.8.7b)
breadboards: 1

parts:
  Part1 = Arduino Pro Mini v13
  Part2 = FTDI Basic Programmer
  IC1 = AD8232 HeartRate Monitor [part_number=SEN-12650 chip_label=IC package="DIP (Dual Inline) [THT]"]

nets:
  N1: Part1.DTR, Part2.DTR
  N2: Part1.D0/TX, Part2.RXI
  N3: Part1.D1/RX, Part2.TXO
  VCC: Part1.VCC, Part2.POWER, IC1.3.3v
  GND: Part1.GND, Part2.CTS, Part2.GND, IC1.GND
  N4: Part1.A0, IC1.OUTPUT
  N5: Part1.D11_PWM/MOSI, IC1.LO+
  N6: Part1.D10_PWM/SS, IC1.LO-

custom parts:
  AD8232 HeartRate Monitor: A DIP stand-in part for whatever IC you want. With 10 pins on a 600mil dual inline package (DIP) footprint.
